# Fritzing sketch schematic (saved by Fritzing 0.9.4)
breadboards: 1

parts:
  U1 = ESP8266 NodeMCU LoLin module
  10k = Temperature Sensor (Thermistor) [thermistor_type=NTC package=THT]
  Q1 = MOSFET-NCHANNEL [package=to220v]
  LiPo_10k_mAH = LIPO-2000mAh [package=lipo-2000]
  Part1 = Solar Panel [package="Renogy 50 Watts 12 Volt Monocrystalline Bendable Solar Panel"]
  Q2 = MOSFET-NCHANNEL [package=to220v]
  12V_to_5V_Converter = IC, DIP package, 4 pins
  130k = Resistor upright [package=THT]
  10k_2 = Resistor upright [package=THT]
  DHT22 = IC, SIP package, 4 pins
  Raspberry_Pi_B_rev1 = Raspberry Pi B rev1
  Q3 = MOSFET-NCHANNEL [package=to220v]
  LiPo_Charger = TP4056 [chip_label=DFR0446 package="DIP (Dual Inline) [THT]"]

nets:
  N1: U1.D0, U1.RST
  N2: U1.D1, DHT22.pin2
  N3: U1.D2, Q3.G
  N4: U1.D3, Raspberry_Pi_B_rev1.GPIO_4
  N5: U1.D4, Raspberry_Pi_B_rev1.GPIO_17
  N6: U1.3V3, 10k.pin_1, DHT22.pin1
  N7: U1.D5, Q1.G
  N8: U1.D6, Q2.G
  N9: U1.Vin, Q3.D, LiPo_Charger.pin3
  GND: U1.GND, 10k_2.Pin_1, DHT22.pin4, Raspberry_Pi_B_rev1.GND, LiPo_Charger.pin6
  N10: U1.A0, Q1.S, Q2.S
  N11: 10k.pin_0, Q2.D, 10k_2.Pin_0
  N12: Q1.D, 130k.Pin_1
  N13: LiPo_10k_mAH.+, 130k.Pin_0, LiPo_Charger.pin4
  N14: LiPo_10k_mAH.-, LiPo_Charger.pin5
  N15: Part1.Connector_1, 12V_to_5V_Converter.pin1
  N16: Part1.Connector_2, 12V_to_5V_Converter.pin2
  N17: 12V_to_5V_Converter.pin3, LiPo_Charger.pin2
  N18: 12V_to_5V_Converter.pin4, LiPo_Charger.pin1
  N19: Raspberry_Pi_B_rev1.5V, Q3.S

notes:
  GPIO4: LOW initiates shutdown
  GPIO17: LOW in halted state
  measures °C outside
  measures °C inside

custom parts:
  ESP8266 NodeMCU LoLin module: ESP8266 based NodeMCU
  Solar Panel: Renogy 50 Watts 12 Volt Solar Panel
  Resistor upright: A generic upright standing resistor (0.25W)
  TP4056: A DIP stand-in part for whatever IC you want. With 6 pins on a 300mil dual inline package (DIP) footprint.
